# Fritzing sketch fsae_combustao (saved by Fritzing 0.9.2b)
breadboards: 1

parts:
  Componente1 = Arduino Mega 2560 (Rev3)
  U1 = U-Blox Neo 6M [package="NEO 6M"]
  PCB2 = RTC_DS1302_module  # not connected
  Componente2 = LC Studio SD Card Module
  Componente3 = Arduino Xbee Libellium Shield  # not connected
  U2 = XBee  # not connected
  GY1 = MPU-6050 Board GY-521 [form="♀ (female)" package=THT]  # not connected

nets:
  3V3: Componente1.3V3, Componente2.3V3
  5V: Componente1.5V, U1.VCC
  GND: Componente1.GND, U1.GND, Componente2.GND

custom parts:
  RTC_DS1302_module: Arduino module DS1302 SPI Real Time Clock
  LC Studio SD Card Module: The LC Studio SD card module serves as an interface to an SD card. The module works at 3.3 volts and 5 volts. The SPI (Serial Peripheral Interface) protocol is used for communicating with the module.
  MPU-6050 Board GY-521: Acelerometro y Giroscopio MPU-6050 Board GY-521
